# Fritzing sketch arduinoSchem (saved by Fritzing 0.9.3b)
circuit board: 8.46667cm x 5.64444cm
breadboards: 2

parts:
  Composant1 = Arduino Mega 2560 (Rev3)
  B3 = Pushbutton [package="[THT]"]
  B1 = Pushbutton [package="[THT]"]
  B2 = Pushbutton [package="[THT]"]
  SS2 = 7-SEGMENT-4DIGIT-YOUNGSUN [package=7-segment-4digit-youngsun]
  B4 = Pushbutton [package="[THT]"]
  L6 = LED - 5mm [color="Red (633nm)" package="5 mm [THT]"]
  L7 = LED - 5mm [color="Red (633nm)" package="5 mm [THT]"]
  L5 = LED - 5mm [color="Red (633nm)" package="5 mm [THT]"]
  L1 = LED - 5mm [color="Red (633nm)" package="5 mm [THT]"]
  L2 = LED - 5mm [color="Red (633nm)" package="5 mm [THT]"]
  L3 = LED - 5mm [color="Red (633nm)" package="5 mm [THT]"]
  L4 = LED - 5mm [color="Red (633nm)" package="5 mm [THT]"]
  R1 = Resistor [tolerance=±5% resistance=220 package=THT]
  R2 = Resistor [tolerance=±5% resistance=220 package=THT]
  R3 = Resistor [tolerance=±5% resistance=220 package=THT]
  R5 = Resistor [tolerance=±5% resistance=220 package=THT]
  R6 = Resistor [tolerance=±5% resistance=220 package=THT]
  R7 = Resistor [tolerance=±5% resistance=220 package=THT]
  R8 = Resistor [tolerance=±5% resistance=220 package=THT]
  R9 = Resistor [tolerance=±5% resistance=220 package=THT]
  R12 = Resistor [tolerance=±5% resistance=10k package=THT]
  R13 = Resistor [tolerance=±5% resistance=10k package=THT]
  R14 = Resistor [tolerance=±5% resistance=10k package=THT]
  Composant3 = NRF24L01
  C1 = Ceramic Capacitor [capacitance=100nF package="100 mil [THT, multilayer]"]
  SS1 = 7-SEGMENT-4DIGIT-YOUNGSUN [package=7-segment-4digit-youngsun-longpads]
  R15 = Resistor [tolerance=±5% resistance=220 package=THT]
  R17 = Resistor [tolerance=±5% resistance=220 package=THT]
  R18 = Resistor [tolerance=±5% resistance=220 package=THT]
  R19 = Resistor [tolerance=±5% resistance=220 package=THT]
  R20 = Resistor [tolerance=±5% resistance=220 package=THT]
  R21 = Resistor [tolerance=±5% resistance=220 package=THT]
  R22 = Resistor [tolerance=±5% resistance=220 package=THT]
  R23 = Resistor [tolerance=±5% resistance=220 package=THT]
  R24 = Resistor [tolerance=±5% resistance=220 package=THT]
  R25 = Resistor [tolerance=±5% resistance=220 package=THT]
  R26 = Resistor [tolerance=±5% resistance=220 package=THT]
  R27 = Resistor [tolerance=±5% resistance=220 package=THT]
  R28 = Resistor [tolerance=±5% resistance=220 package=THT]
  R29 = Resistor [tolerance=±5% resistance=220 package=THT]
  Raspberry_Pi1 = Raspberry Pi B rev2
  Composant4 = NRF24L01

nets:
  N1: Composant1.D19/RX1, Composant3.CE
  GND: Composant1.GND, L6.cathode, L7.cathode, L5.cathode, L1.cathode, L2.cathode, L3.cathode, L4.cathode, R9.Pin_1, R12.Pin_0, R13.Pin_0, R14.Pin_0, Composant3.GND, C1.0
  3V3: Composant1.3V3, Composant3.VCC, C1.1
  N2: Composant1.5V, B3.Pin_3, B3.Pin_4, B1.Pin_3, B1.Pin_4, B2.Pin_3, B2.Pin_4, B4.Pin_3, B4.Pin_4
  N3: Composant1.D45, R3.Pin_1
  N4: Composant1.D47, R7.Pin_1
  N5: Composant1.D50, Composant3.MISO
  N6: Composant1.D51, Composant3.MOSI
  N7: Composant1.D52, Composant3.SCK
  N8: Composant1.D53, Composant3.CSN
  N9: B3.Pin_1, B3.Pin_2, R12.Pin_1
  N10: B1.Pin_1, B1.Pin_2, R14.Pin_1
  N11: B2.Pin_1, B2.Pin_2, R13.Pin_1
  N12: SS2.D, R24.Pin_1
  N13: SS2.E, R23.Pin_0
  N14: SS2.F, R28.Pin_0
  N15: SS2.C, R27.Pin_1
  N16: SS2.A, R26.Pin_1
  N17: SS2.G, R25.Pin_1
  N18: SS2.B, R29.Pin_0
  N19: B4.Pin_1, B4.Pin_2, R9.Pin_0
  N20: L6.anode, R5.Pin_0
  N21: L7.anode, R6.Pin_0
  N22: L5.anode, R7.Pin_0
  N23: L1.anode, R1.Pin_0
  N24: L2.anode, R2.Pin_1
  N25: L3.anode, R3.Pin_0
  N26: L4.anode, R8.Pin_0
  N27: SS1.D, R20.Pin_1
  N28: SS1.E, R21.Pin_0
  N29: SS1.F, R15.Pin_0
  N30: SS1.C, R17.Pin_1
  N31: SS1.A, R18.Pin_1
  N32: SS1.G, R19.Pin_1
  N33: SS1.B, R22.Pin_1
  3V3_2: Raspberry_Pi1.3V3, Composant4.VCC
  GND_2: Raspberry_Pi1.GND, Composant4.GND
  N34: Raspberry_Pi1.GPIO_10, Composant4.MOSI
  N35: Raspberry_Pi1.GPIO_9, Composant4.MISO
  N36: Raspberry_Pi1.GPIO_25, Composant4.CE
  N37: Raspberry_Pi1.GPIO_11, Composant4.SCK
  N38: Raspberry_Pi1.GPIO_8, Composant4.CSN
